// Logisim project 817570-multi2.circ as structural Verilog: 3 circuits, main circuit main
module main (
);

  wire AB_en, ALUout_en, Branch, clk, IR_en, MDR_en, MemRd, MemWr, PC_en, RegDst, RegWr, reset;
  wire [1:0] Mem2Reg;
  wire [2:0] OP;
  wire [3:0] rom_2_data;
  wire [4:0] RA, RB, RW;
  wire [4:2] RD;
  wire [4:4] comparator_1_eq;
  wire [6:3] register_7_q;
  wire [7:0] adder_1_out, multiplexer_2_out, register_1_q;
  wire [15:0] Imm;
  wire [31:0] adder_2_out, br32_1_busa, br32_1_busb, busA, busB, busW, Imm32, MDR, ram_1_data, register_4_q,
       rom_1_data;

  Button button_1 (.out(reset));
  Clock clock_1 (.out(clk));
  Adder adder_1 (.a(register_1_q), .b(8'h1), .out(adder_1_out));  // open: cin, cout
  assign Imm32 = {{16{Imm[15]}}, Imm};  // Bit_Extender bit_extender_1
  Multiplexer #(.width(5), .disabled(0), .enable("false")) multiplexer_1 (
    .in0(RB), .in1({RD, Imm[15:14]}), .out(RW), .sel(RegDst));
  // RTL1_Viewer rtl1_viewer_1: pin names not known; wires that end beside it: busW, RW, RegWr
  // RTL2_Viewer rtl2_viewer_1: pin names not known; wires that end beside it: MDR_en, MemWr, busB
  Multiplexer #(.width(8), .disabled(0), .enable("false")) multiplexer_2 (
    .in0(adder_1_out), .in1(Imm[7:0]), .out(multiplexer_2_out), .sel(Branch));
  BR32 br32_1 (
    .RA(RA), .RB(RB), .RW(RW), .RegWr(RegWr), .busW(busW), .clk(clk), .reset(reset), .busA(br32_1_busa),
    .busB(br32_1_busb));
  Register register_1 (.D(multiplexer_2_out), .en(PC_en), .Q(register_1_q), .clk(clk), .clr(reset));
  Register #(.width(32)) register_2 (.D(br32_1_busa), .en(AB_en), .Q(busA), .clk(clk), .clr(reset));
  Register #(.width(32)) register_3 (.D(br32_1_busb), .en(AB_en), .Q(busB), .clk(clk), .clr(reset));
  Adder #(.width(32)) adder_2 (.a(busA), .b(busB), .out(adder_2_out));  // open: cin, cout
  // tty_ctrl tty_ctrl_1: pin names not known
  // TTY tty_1: pin names not known; wires that end beside it: MemWr, clk
  ROM #(.dataWidth(32)) rom_1 (.addr(register_1_q), .data(rom_1_data));  // open: sel
  Register #(.width(32)) register_4 (.D(adder_2_out), .en(ALUout_en), .Q(register_4_q), .clk(clk), .clr(reset));
  Register #(.width(32)) register_5 (.D(rom_1_data), .en(IR_en), .Q({OP, RA, RB, RD, Imm}), .clk(clk), .clr(reset));
  Multiplexer #(.select(2), .width(32), .disabled(0), .enable("false")) multiplexer_3 (
    .in0(register_4_q), .in1(MDR), .in2(Imm32), .out(busW), .sel(Mem2Reg));  // open: in3
  RAM #(.addrWidth(16), .dataWidth(32), .bus("separate")) ram_1 (
    .addr(busA[15:0]), .din(busB), .data(ram_1_data), .str(MemWr), .clk(clk), .ld(MemRd));  // open: sel, clr
  Register #(.width(32)) register_6 (.D(ram_1_data), .Q(MDR), .clk(clk), .clr(reset));  // open: en
  ROM #(.addrWidth(7), .dataWidth(4)) rom_2 (.addr({register_7_q, OP}), .data(rom_2_data));  // open: sel
  Register #(.width(4)) register_7 (.D(rom_2_data), .Q(register_7_q), .clk(clk), .clr(reset));  // open: en
  Comparator #(.width(32)) comparator_1 (.a(busA), .b(busB), .eq(comparator_1_eq[4]));  // open: gt, lt
  ROM #(.addrWidth(5), .dataWidth(12)) rom_3 (
    .addr({comparator_1_eq[4], register_7_q}),
    .data({PC_en, IR_en, AB_en, ALUout_en, MDR_en, RegDst, RegWr, Branch, MemWr, MemRd, Mem2Reg}));  // open: sel

  // Other names for the same wires on the sheet: RD[1:0] = Imm[15:14]

  // Notes on the sheet:
  //   contents of rom_1 (hex, n*v repeats v):
  //   20000000 20080047 20200006 20280001 41208000 a110000a 61180000 40180000 41284000 a5280005 2037ffff
  //   20380000 67380000 a0380014 2048004e 86480000 2048004f 86480000 20480020 86480000 2048004f 86480000
  //   2048004b 86480000 a5280018
  //   contents of rom_2 (hex, n*v repeats v):
  //   6*1 0 0 0 2 3 5 7 8 12*0 4 16*0 6
  //   contents of rom_3 (hex, n*v repeats v):
  //   400 200 822 100 860 84 821 808 800 7*0 400 200 822 100 860 84 821 808 810
endmodule

module BR4 (
  input  RegWr,
  input  [31:0] busW,
  input  [1:0] RA,
  input  [1:0] RB,
  input  [1:0] RW,
  input  clk,
  input  reset,
  output [31:0] busA,
  output [31:0] busB
);

  wire Reg0_en, Reg1_en, Reg2_en, Reg3_en;
  wire [31:0] Reg0_out, Reg1_out, Reg2_out, Reg3_out;

  Decoder #(.select(2), .disabled(0)) decoder_1 (
    .out0(Reg0_en), .out1(Reg1_en), .out2(Reg2_en), .out3(Reg3_en), .sel(RW), .en(RegWr));
  Register #(.width(32)) register_1 (.D(busW), .en(Reg0_en), .Q(Reg0_out), .clk(clk), .clr(reset));
  Register #(.width(32)) register_2 (.D(busW), .en(Reg1_en), .Q(Reg1_out), .clk(clk), .clr(reset));
  Register #(.width(32)) register_3 (.D(busW), .en(Reg2_en), .Q(Reg2_out), .clk(clk), .clr(reset));
  Register #(.width(32)) register_4 (.D(busW), .en(Reg3_en), .Q(Reg3_out), .clk(clk), .clr(reset));
  Multiplexer #(.select(2), .width(32), .enable("false")) multiplexer_1 (
    .in0(Reg0_out), .in1(Reg1_out), .in2(Reg2_out), .in3(Reg3_out), .out(busA), .sel(RA));
  Multiplexer #(.select(2), .width(32), .enable("false")) multiplexer_2 (
    .in0(Reg0_out), .in1(Reg1_out), .in2(Reg2_out), .in3(Reg3_out), .out(busB), .sel(RB));
endmodule

module BR32 (
  input  RegWr,
  input  [31:0] busW,
  input  [4:0] RA,
  input  [4:0] RB,
  input  [4:0] RW,
  input  clk,
  input  reset,
  output [31:0] busA,
  output [31:0] busB
);

  wire RegWr_BR_0, RegWr_BR_1, RegWr_BR_2, RegWr_BR_3, RegWr_BR_4, RegWr_BR_5, RegWr_BR_6, RegWr_BR_7;
  wire [31:0] BR_0_A_Out, BR_0_B_Out, BR_1_A_Out, BR_1_B_Out, BR_2_A_Out, BR_2_B_Out, BR_3_A_Out, BR_3_B_Out,
       BR_4_A_Out, BR_4_B_Out, BR_5_A_Out, BR_5_B_Out, BR_6_A_Out, BR_6_B_Out, BR_7_A_Out, BR_7_B_Out;

  Decoder #(.select(3), .disabled(0)) decoder_1 (
    .out0(RegWr_BR_0), .out1(RegWr_BR_1), .out2(RegWr_BR_2), .out3(RegWr_BR_3), .out4(RegWr_BR_4),
    .out5(RegWr_BR_5), .out6(RegWr_BR_6), .out7(RegWr_BR_7), .sel(RW[4:2]), .en(RegWr));
  BR4 br4_1 (
    .RA(RA[1:0]), .RB(RB[1:0]), .RW(RW[1:0]), .RegWr(RegWr_BR_0), .busW(busW), .clk(clk), .reset(reset),
    .busA(BR_0_A_Out), .busB(BR_0_B_Out));
  BR4 br4_2 (
    .RA(RA[1:0]), .RB(RB[1:0]), .RW(RW[1:0]), .RegWr(RegWr_BR_1), .busW(busW), .clk(clk), .reset(reset),
    .busA(BR_1_A_Out), .busB(BR_1_B_Out));
  BR4 br4_3 (
    .RA(RA[1:0]), .RB(RB[1:0]), .RW(RW[1:0]), .RegWr(RegWr_BR_2), .busW(busW), .clk(clk), .reset(reset),
    .busA(BR_2_A_Out), .busB(BR_2_B_Out));
  BR4 br4_4 (
    .RA(RA[1:0]), .RB(RB[1:0]), .RW(RW[1:0]), .RegWr(RegWr_BR_3), .busW(busW), .clk(clk), .reset(reset),
    .busA(BR_3_A_Out), .busB(BR_3_B_Out));
  BR4 br4_5 (
    .RA(RA[1:0]), .RB(RB[1:0]), .RW(RW[1:0]), .RegWr(RegWr_BR_4), .busW(busW), .clk(clk), .reset(reset),
    .busA(BR_4_A_Out), .busB(BR_4_B_Out));
  BR4 br4_6 (
    .RA(RA[1:0]), .RB(RB[1:0]), .RW(RW[1:0]), .RegWr(RegWr_BR_5), .busW(busW), .clk(clk), .reset(reset),
    .busA(BR_5_A_Out), .busB(BR_5_B_Out));
  BR4 br4_7 (
    .RA(RA[1:0]), .RB(RB[1:0]), .RW(RW[1:0]), .RegWr(RegWr_BR_6), .busW(busW), .clk(clk), .reset(reset),
    .busA(BR_6_A_Out), .busB(BR_6_B_Out));
  BR4 br4_8 (
    .RA(RA[1:0]), .RB(RB[1:0]), .RW(RW[1:0]), .RegWr(RegWr_BR_7), .busW(busW), .clk(clk), .reset(reset),
    .busA(BR_7_A_Out), .busB(BR_7_B_Out));
  Multiplexer #(.select(3), .width(32), .enable("false")) multiplexer_1 (
    .in0(BR_0_A_Out), .in1(BR_1_A_Out), .in2(BR_2_A_Out), .in3(BR_3_A_Out), .in4(BR_4_A_Out),
    .in5(BR_5_A_Out), .in6(BR_6_A_Out), .in7(BR_7_A_Out), .out(busA), .sel(RA[4:2]));
  Multiplexer #(.select(3), .width(32), .enable("false")) multiplexer_2 (
    .in0(BR_0_B_Out), .in1(BR_1_B_Out), .in2(BR_2_B_Out), .in3(BR_3_B_Out), .in4(BR_4_B_Out),
    .in5(BR_5_B_Out), .in6(BR_6_B_Out), .in7(BR_7_B_Out), .out(busB), .sel(RB[4:2]));

  // Other names for the same wires on the sheet: RA_BR4[1:0] = RA[1:0]; RA_BR16[2:0] = RA[4:2]; RB_BR4[1:0] = RB[1:0];
  //   RB_BR16[2:0] = RB[4:2]; RW_BR4[1:0] = RW[1:0]; RW_BR16[2:0] = RW[4:2]
endmodule
