// Logisim project 817570-multi.circ as structural Verilog: 3 circuits, main circuit main
module main (
);

  wire clk, reset;
  wire [3:0] rom_1_data;
  wire [4:0] register_1_q;
  wire [7:0] adder_1_out, PC_q;
  wire [30:0] rom_2_data;
  wire [31:0] adder_2_out, bit_extender_1_out, br32_1_busa, br32_1_busb, register_2_q, register_3_q,
       register_4_q, rtl1_viewer_1_p1;

  Button button_1 (.out(reset));
  Clock clock_1 (.out(clk));
  Adder adder_1 (.a(PC_q), .b(8'h1), .out(adder_1_out), .cin(1'b0));  // open: cout
  Register PC (.D(adder_1_out), .en(rom_1_data[0]), .Q(PC_q), .clk(clk), .clr(reset));
  ROM #(.addrWidth(5), .dataWidth(4)) rom_1 (.addr(register_1_q), .data(rom_1_data));  // open: sel
  ROM #(.dataWidth(32)) rom_2 (.addr(PC_q), .data({register_1_q[4], rom_2_data}));  // open: sel
  Register #(.width(4)) register_1 (.D(rom_1_data), .en(1'b1), .Q(register_1_q[3:0]), .clk(clk), .clr(reset));
  BR32 br32_1 (
    .RA(rom_2_data[30:26]), .RB(rom_2_data[25:21]), .RW(rom_2_data[20:16]), .RegWr(rom_1_data[0]),
    .busW(rtl1_viewer_1_p1), .clk(clk), .reset(reset), .busA(br32_1_busa), .busB(br32_1_busb));
  assign bit_extender_1_out = {{16{rom_2_data[15]}}, rom_2_data[15:0]};  // Bit_Extender bit_extender_1
  Register #(.width(32)) register_2 (.D(br32_1_busa), .en(rom_1_data[3]), .Q(register_2_q), .clk(clk), .clr(reset));
  Register #(.width(32)) register_3 (.D(br32_1_busb), .en(rom_1_data[3]), .Q(register_3_q), .clk(clk), .clr(reset));
  Adder #(.width(32)) adder_2 (.a(register_2_q), .b(register_3_q), .out(adder_2_out), .cin(1'b0));  // open: cout
  Register #(.width(32)) register_4 (.D(adder_2_out), .en(rom_1_data[2]), .Q(register_4_q), .clk(clk), .clr(reset));
  // RTL1_Viewer rtl1_viewer_1: pin names not known; wires that end beside it: rtl1_viewer_1_p1, rom_2_data[20:16], rom_1_data[0]
  Multiplexer #(.width(32), .disabled(0), .enable("false")) multiplexer_1 (
    .in0(register_4_q), .in1(bit_extender_1_out), .out(rtl1_viewer_1_p1), .sel(rom_1_data[1]));

  // Notes on the sheet:
  //   contents of rom_1 (hex, n*v repeats v):
  //   8 8 0 0 1 0 0 0 4 7*0 8 0 0 8 4*0 3
  //   contents of rom_2 (hex, n*v repeats v):
  //   80000000 80012710 80020000 80030000 80041b58 800501f4 80060046 80070000 200000 400000 600000 800000
  //   a00000 c00000 e00000
endmodule

module BR4 (
  input  [31:0] busW,
  input  RegWr,
  input  [1:0] RA,
  input  clk,
  input  reset,
  input  [1:0] RB,
  input  [1:0] RW,
  output [31:0] busA,
  output [31:0] busB
);

  wire decoder_1_out0, decoder_1_out1, decoder_1_out2, decoder_1_out3;
  wire [31:0] register_1_q, register_2_q, register_3_q, register_4_q;

  Decoder #(.select(2), .disabled(0)) decoder_1 (
    .out0(decoder_1_out0), .out1(decoder_1_out1), .out2(decoder_1_out2), .out3(decoder_1_out3), .sel(RW),
    .en(RegWr));
  Register #(.width(32)) register_1 (.D(busW), .en(decoder_1_out0), .Q(register_1_q), .clk(clk), .clr(reset));
  Register #(.width(32)) register_2 (.D(busW), .en(decoder_1_out1), .Q(register_2_q), .clk(clk), .clr(reset));
  Register #(.width(32)) register_3 (.D(busW), .en(decoder_1_out2), .Q(register_3_q), .clk(clk), .clr(reset));
  Register #(.width(32)) register_4 (.D(busW), .en(decoder_1_out3), .Q(register_4_q), .clk(clk), .clr(reset));
  Multiplexer #(.select(2), .width(32), .enable("false")) multiplexer_1 (
    .in0(register_1_q), .in1(register_2_q), .in2(register_3_q), .in3(register_4_q), .out(busA), .sel(RA));
  Multiplexer #(.select(2), .width(32), .enable("false")) multiplexer_2 (
    .in0(register_1_q), .in1(register_2_q), .in2(register_3_q), .in3(register_4_q), .out(busB), .sel(RB));
endmodule

// BR
module BR32 (
  input  [31:0] busW,
  input  RegWr,
  input  clk,
  input  reset,
  input  [4:0] RA,
  input  [4:0] RB,
  input  [4:0] RW,
  output [31:0] busA,
  output [31:0] busB
);

  wire decoder_1_out0, decoder_1_out1, decoder_1_out2, decoder_1_out3, decoder_1_out4, decoder_1_out5,
       decoder_1_out6, decoder_1_out7;
  wire [31:0] br4_1_busa, br4_1_busb, br4_2_busa, br4_2_busb, br4_3_busa, br4_3_busb, br4_4_busa, br4_4_busb,
       br4_5_busa, br4_5_busb, br4_6_busa, br4_6_busb, br4_7_busa, br4_7_busb, br4_8_busa, br4_8_busb;

  Decoder #(.select(3), .disabled(0)) decoder_1 (
    .out0(decoder_1_out0), .out1(decoder_1_out1), .out2(decoder_1_out2), .out3(decoder_1_out3),
    .out4(decoder_1_out4), .out5(decoder_1_out5), .out6(decoder_1_out6), .out7(decoder_1_out7),
    .sel(RW[4:2]), .en(RegWr));
  BR4 br4_1 (
    .RA(RA[1:0]), .RB(RB[1:0]), .RW(RW[1:0]), .RegWr(decoder_1_out0), .busW(busW), .clk(clk), .reset(reset),
    .busA(br4_1_busa), .busB(br4_1_busb));
  BR4 br4_2 (
    .RA(RA[1:0]), .RB(RB[1:0]), .RW(RW[1:0]), .RegWr(decoder_1_out1), .busW(busW), .clk(clk), .reset(reset),
    .busA(br4_2_busa), .busB(br4_2_busb));
  BR4 br4_3 (
    .RA(RA[1:0]), .RB(RB[1:0]), .RW(RW[1:0]), .RegWr(decoder_1_out2), .busW(busW), .clk(clk), .reset(reset),
    .busA(br4_3_busa), .busB(br4_3_busb));
  BR4 br4_4 (
    .RA(RA[1:0]), .RB(RB[1:0]), .RW(RW[1:0]), .RegWr(decoder_1_out3), .busW(busW), .clk(clk), .reset(reset),
    .busA(br4_4_busa), .busB(br4_4_busb));
  BR4 br4_5 (
    .RA(RA[1:0]), .RB(RB[1:0]), .RW(RW[1:0]), .RegWr(decoder_1_out4), .busW(busW), .clk(clk), .reset(reset),
    .busA(br4_5_busa), .busB(br4_5_busb));
  BR4 br4_6 (
    .RA(RA[1:0]), .RB(RB[1:0]), .RW(RW[1:0]), .RegWr(decoder_1_out5), .busW(busW), .clk(clk), .reset(reset),
    .busA(br4_6_busa), .busB(br4_6_busb));
  BR4 br4_7 (
    .RA(RA[1:0]), .RB(RB[1:0]), .RW(RW[1:0]), .RegWr(decoder_1_out6), .busW(busW), .clk(clk), .reset(reset),
    .busA(br4_7_busa), .busB(br4_7_busb));
  BR4 br4_8 (
    .RA(RA[1:0]), .RB(RB[1:0]), .RW(RW[1:0]), .RegWr(decoder_1_out7), .busW(busW), .clk(clk), .reset(reset),
    .busA(br4_8_busa), .busB(br4_8_busb));
  Multiplexer #(.select(3), .width(32), .enable("false")) multiplexer_1 (
    .in0(br4_1_busa), .in1(br4_2_busa), .in2(br4_3_busa), .in3(br4_4_busa), .in4(br4_5_busa),
    .in5(br4_6_busa), .in6(br4_7_busa), .in7(br4_8_busa), .out(busA), .sel(RA[4:2]));
  Multiplexer #(.select(3), .width(32), .enable("false")) multiplexer_2 (
    .in0(br4_1_busb), .in1(br4_2_busb), .in2(br4_3_busb), .in3(br4_4_busb), .in4(br4_5_busb),
    .in5(br4_6_busb), .in6(br4_7_busb), .in7(br4_8_busb), .out(busB), .sel(RB[4:2]));
endmodule
