// Logisim project 817570-multi2.circ as structural Verilog: 3 circuits, main circuit main
module main (
);

  wire AB_en, ALUOut_en, and_1_out, Branch, clk, comparator_1_eq, IR_en, MDR_en, MemRd, MemWr, PC_en, RegDst,
       RegWr, reset;
  wire [1:0] Mem2Reg;
  wire [2:0] Instr;
  wire [4:0] RW;
  wire [7:0] PC_1, PC_q, PC_star;
  wire [11:0] register_1_q, rom_2_data;
  wire [28:0] IR_q;
  wire [31:0] A, adder_2_out, ALUOut_q, B, br32_1_busa, br32_1_busb, busW, Ext_Inm, MDR_q, ram_1_data,
       rom_1_data;

  Button button_1 (.out(reset));
  Clock clock_1 (.out(clk));
  Register PC (.D(PC_star), .en(PC_en), .Q(PC_q), .clk(clk), .clr(reset));
  // RTL1_Viewer rtl1_viewer_1: pin names not known; wires that end beside it: busW, RW, RegWr
  Adder adder_1 (.a(PC_q), .b(8'h1), .out(PC_1), .cin(1'b0));  // open: cout
  ROM #(.dataWidth(32)) rom_1 (.addr(PC_q), .data(rom_1_data));  // open: sel
  ROM #(.addrWidth(15), .dataWidth(12)) rom_2 (.addr({Instr, register_1_q}), .data(rom_2_data));  // open: sel
  Register #(.width(32)) IR (.D(rom_1_data), .en(IR_en), .Q({Instr, IR_q}), .clk(clk), .clr(reset));
  Register #(.width(12)) register_1 (.D(rom_2_data), .Q(register_1_q), .clk(clk), .clr(reset));  // open: en
  // tty_ctrl tty_ctrl_1: pin names not known
  // TTY tty_1: pin names not known; wires that end beside it: A[15:0], MemWr, B[6:0], clk
  Multiplexer #(.width(5), .disabled(0), .enable("false")) multiplexer_1 (
    .in0(IR_q[23:19]), .in1(IR_q[18:14]), .out(RW), .sel(RegDst));
  assign Ext_Inm = {{16{IR_q[15]}}, IR_q[15:0]};  // Bit_Extender bit_extender_1
  // RTL2_Viewer rtl2_viewer_1: pin names not known; wires that end beside it: MDR_en, A[15:0], MemWr, B
  BR32 br32_1 (
    .RA(IR_q[28:24]), .RB(IR_q[23:19]), .RW(RW), .RegWr(RegWr), .busW(busW), .clk(clk), .reset(reset),
    .busA(br32_1_busa), .busB(br32_1_busb));
  ROM #(.addrWidth(15), .dataWidth(12)) rom_3 (
    .addr({Instr, register_1_q}),
    .data({PC_en, IR_en, AB_en, ALUOut_en, MDR_en, RegDst, RegWr, Branch, MemWr, MemRd, Mem2Reg}));  // open: sel
  Register #(.width(32)) u_A (.D(br32_1_busa), .en(AB_en), .Q(A), .clk(clk), .clr(reset));
  Register #(.width(32)) u_B (.D(br32_1_busb), .en(AB_en), .Q(B), .clk(clk), .clr(reset));
  Comparator #(.width(32)) comparator_1 (.a(A), .b(B), .eq(comparator_1_eq));  // open: gt, lt
  Adder #(.width(32)) adder_2 (.a(A), .b(B), .out(adder_2_out), .cin(1'b0));  // open: cout
  and and_1 (and_1_out, comparator_1_eq, Branch);
  RAM #(.addrWidth(16), .dataWidth(32), .bus("separate")) ram_1 (
    .addr(A[15:0]), .din(B), .data(ram_1_data), .str(MemWr), .clk(clk), .ld(MemRd), .clr(reset));  // open: sel
  Register #(.width(32)) ALUOut (.D(adder_2_out), .en(ALUOut_en), .Q(ALUOut_q), .clk(clk), .clr(reset));
  Multiplexer #(.width(8), .disabled(0), .enable("false")) multiplexer_2 (
    .in0(PC_1), .in1(Ext_Inm[7:0]), .out(PC_star), .sel(and_1_out));
  Register #(.width(32)) MDR (.D(ram_1_data), .en(MDR_en), .Q(MDR_q), .clk(clk), .clr(reset));
  Multiplexer #(.select(2), .width(32), .disabled(0), .enable("false")) multiplexer_3 (
    .in0(MDR_q), .in1(ALUOut_q), .in2(Ext_Inm), .out(busW), .sel(Mem2Reg));  // open: in3

  // Other names for the same wires on the sheet: A_15_0[15:0] = A[15:0]; D_in[31:0] = B

  // Notes on the sheet:
  //   contents of rom_1 (hex, n*v repeats v):
  //   46 80000 100000 180006 200000 280001 300000 40ffff 48000a 49380000 24290000 20280000 40100000
  //   21104000 83200010 8528000a 66080000 81380018 48004e 68480000 48004f 68480000 480020 68480000 48004f
  //   68480000 48004b 68480000 8528001c
  //   Fetch
  //   contents of rom_2 (hex, n*v repeats v):
  //   400 511*0 822 511*0 200 1057*0 400 2269*0 861 255*0 100 511*0 200 1120*0 400 2082*0 820 379*0 84
  //   511*0 200 1055*0 400 2527*0 808 511*0 200 1031*0 400 2551*0 810 511*0 200 1039*0 400 3055*0 800
  //   1023*0 400
  //   Unidad de Control
  //   Decode
  //   Writeback
  //   contents of rom_3 (hex, n*v repeats v):
  //   512*0 200 511*0 400 1057*0 822 2269*0 100 255*0 200 511*0 400 1120*0 861 2082*0 84 379*0 200 511*0
  //   400 1055*0 820 2527*0 200 511*0 400 1031*0 808 2551*0 200 511*0 400 1039*0 810 3055*0 400 1023*0 800
  //   Control de Branch (Execute)
  //   Memory
  //   Execute
  //   Writeback
endmodule

module BR4 (
  input  [31:0] busW,
  input  RegWr,
  input  [1:0] RA,
  input  clk,
  input  reset,
  input  [1:0] RB,
  input  [1:0] RW,
  output [31:0] busA,
  output [31:0] busB
);

  wire decoder_1_out0, decoder_1_out1, decoder_1_out2, decoder_1_out3;
  wire [31:0] register_1_q, register_2_q, register_3_q, register_4_q;

  Decoder #(.select(2), .disabled(0)) decoder_1 (
    .out0(decoder_1_out0), .out1(decoder_1_out1), .out2(decoder_1_out2), .out3(decoder_1_out3), .sel(RW),
    .en(RegWr));
  Register #(.width(32)) register_1 (.D(busW), .en(decoder_1_out0), .Q(register_1_q), .clk(clk), .clr(reset));
  Register #(.width(32)) register_2 (.D(busW), .en(decoder_1_out1), .Q(register_2_q), .clk(clk), .clr(reset));
  Register #(.width(32)) register_3 (.D(busW), .en(decoder_1_out2), .Q(register_3_q), .clk(clk), .clr(reset));
  Register #(.width(32)) register_4 (.D(busW), .en(decoder_1_out3), .Q(register_4_q), .clk(clk), .clr(reset));
  Multiplexer #(.select(2), .width(32), .enable("false")) multiplexer_1 (
    .in0(register_1_q), .in1(register_2_q), .in2(register_3_q), .in3(register_4_q), .out(busA), .sel(RA));
  Multiplexer #(.select(2), .width(32), .enable("false")) multiplexer_2 (
    .in0(register_1_q), .in1(register_2_q), .in2(register_3_q), .in3(register_4_q), .out(busB), .sel(RB));
endmodule

// BR
module BR32 (
  input  [31:0] busW,
  input  RegWr,
  input  clk,
  input  reset,
  input  [4:0] RA,
  input  [4:0] RB,
  input  [4:0] RW,
  output [31:0] busA,
  output [31:0] busB
);

  wire decoder_1_out0, decoder_1_out1, decoder_1_out2, decoder_1_out3, decoder_1_out4, decoder_1_out5,
       decoder_1_out6, decoder_1_out7;
  wire [31:0] br4_1_busa, br4_1_busb, br4_2_busa, br4_2_busb, br4_3_busa, br4_3_busb, br4_4_busa, br4_4_busb,
       br4_5_busa, br4_5_busb, br4_6_busa, br4_6_busb, br4_7_busa, br4_7_busb, br4_8_busa, br4_8_busb;

  Decoder #(.select(3), .disabled(0)) decoder_1 (
    .out0(decoder_1_out0), .out1(decoder_1_out1), .out2(decoder_1_out2), .out3(decoder_1_out3),
    .out4(decoder_1_out4), .out5(decoder_1_out5), .out6(decoder_1_out6), .out7(decoder_1_out7),
    .sel(RW[4:2]), .en(RegWr));
  BR4 br4_1 (
    .RA(RA[1:0]), .RB(RB[1:0]), .RW(RW[1:0]), .RegWr(decoder_1_out0), .busW(busW), .clk(clk), .reset(reset),
    .busA(br4_1_busa), .busB(br4_1_busb));
  BR4 br4_2 (
    .RA(RA[1:0]), .RB(RB[1:0]), .RW(RW[1:0]), .RegWr(decoder_1_out1), .busW(busW), .clk(clk), .reset(reset),
    .busA(br4_2_busa), .busB(br4_2_busb));
  BR4 br4_3 (
    .RA(RA[1:0]), .RB(RB[1:0]), .RW(RW[1:0]), .RegWr(decoder_1_out2), .busW(busW), .clk(clk), .reset(reset),
    .busA(br4_3_busa), .busB(br4_3_busb));
  BR4 br4_4 (
    .RA(RA[1:0]), .RB(RB[1:0]), .RW(RW[1:0]), .RegWr(decoder_1_out3), .busW(busW), .clk(clk), .reset(reset),
    .busA(br4_4_busa), .busB(br4_4_busb));
  BR4 br4_5 (
    .RA(RA[1:0]), .RB(RB[1:0]), .RW(RW[1:0]), .RegWr(decoder_1_out4), .busW(busW), .clk(clk), .reset(reset),
    .busA(br4_5_busa), .busB(br4_5_busb));
  BR4 br4_6 (
    .RA(RA[1:0]), .RB(RB[1:0]), .RW(RW[1:0]), .RegWr(decoder_1_out5), .busW(busW), .clk(clk), .reset(reset),
    .busA(br4_6_busa), .busB(br4_6_busb));
  BR4 br4_7 (
    .RA(RA[1:0]), .RB(RB[1:0]), .RW(RW[1:0]), .RegWr(decoder_1_out6), .busW(busW), .clk(clk), .reset(reset),
    .busA(br4_7_busa), .busB(br4_7_busb));
  BR4 br4_8 (
    .RA(RA[1:0]), .RB(RB[1:0]), .RW(RW[1:0]), .RegWr(decoder_1_out7), .busW(busW), .clk(clk), .reset(reset),
    .busA(br4_8_busa), .busB(br4_8_busb));
  Multiplexer #(.select(3), .width(32), .enable("false")) multiplexer_1 (
    .in0(br4_1_busa), .in1(br4_2_busa), .in2(br4_3_busa), .in3(br4_4_busa), .in4(br4_5_busa),
    .in5(br4_6_busa), .in6(br4_7_busa), .in7(br4_8_busa), .out(busA), .sel(RA[4:2]));
  Multiplexer #(.select(3), .width(32), .enable("false")) multiplexer_2 (
    .in0(br4_1_busb), .in1(br4_2_busb), .in2(br4_3_busb), .in3(br4_4_busb), .in4(br4_5_busb),
    .in5(br4_6_busb), .in6(br4_7_busb), .in7(br4_8_busb), .out(busB), .sel(RB[4:2]));
endmodule
