// Logisim project 817570-cache.circ as structural Verilog: 1 circuit, main circuit main
module main (
);

  wire and_1_out, block_wr_0, block_wr_1, cache_test4_1_ok, clk, comparator_1_eq, decoder_1_out0, hit,
       mem_en, not_1_out, not_3_out, not_4_out, or_1_out, replace, reset, valid, way, way0_en, way1_en,
       word0_en, word1_en, word2_en, word3_en;
  wire [2:0] cache_test4_1_err;
  wire [3:0] counter_1_q, counter_2_q, tunnel;
  wire [4:0] set;
  wire [6:0] cache_test4_1_ciclo, tag;
  wire [7:0] ram_2_data, ram_3_data;
  wire [31:0] bus, Instr, multiplexer_1_out, multiplexer_2_out, ram_4_data, ram_5_data, ram_6_data,
       ram_7_data, ram_8_data, ram_9_data, ram_10_data, ram_11_data, Word_0_q, Word_1_q, Word_2_q, Word_3_q;

  Clock clock_1 (.out(clk));
  Button button_1 (.out(reset));
  Counter #(.width(4), .max('hf)) counter_1 (
    .count(hit), .Q(counter_1_q), .clk(clk), .clr(reset));  // open: load, D, carry
  not not_1 (not_1_out, replace);
  // Probe on cache_test4_1_err
  // Probe on cache_test4_1_ok
  // Probe on cache_test4_1_ciclo
  cache_test4 cache_test4_1 (
    .clk(clk), .reset(reset), .inst(Instr), .OK(cache_test4_1_ok), .in_3({tag, set, tunnel}),
    .ERR(cache_test4_1_err), .ciclo(cache_test4_1_ciclo), .hit(hit), .way(way), .set(set), .nia(20'hc79a2));
  // Probe on 20'hc79a2
  MP_main main_1 (.dir({tag, set, tunnel}), .mem_en(mem_en), .clk(clk), .reset(reset), .dato(bus));
  ROM #(.addrWidth(4), .dataWidth(16)) rom_1 (.addr(counter_1_q), .data({tag, set, tunnel}));  // open: sel
  RAM #(.addrWidth(5), .dataWidth(1), .bus("separate")) ram_1 (
    .addr(set), .din(not_1_out), .data(replace), .str(valid), .clk(clk), .ld(1'b1), .clr(reset));  // open: sel
  not not_2 (mem_en, hit);
  Counter #(.width(4), .max('hb)) counter_2 (
    .count(mem_en), .Q(counter_2_q), .clk(clk), .clr(reset));  // open: load, D, carry
  Decoder #(.select(4), .disabled(0), .enable("false")) decoder_1 (
    .out0(decoder_1_out0), .out4(word0_en), .out6(word1_en), .out8(word2_en), .out10(word3_en),
    .out11(valid), .sel(counter_2_q));  // open: out1, out2, out3, out5, out7, out9, out12, out13, out14, out15
  RAM #(.addrWidth(5), .bus("separate")) ram_2 (
    .addr(set), .din({valid, tag}), .data(ram_2_data), .str(way0_en), .clk(clk), .ld(1'b1), .clr(reset));  // open: sel
  RAM #(.addrWidth(5), .bus("separate")) ram_3 (
    .addr(set), .din({valid, tag}), .data(ram_3_data), .str(way1_en), .clk(clk), .ld(1'b1), .clr(reset));  // open: sel
  not not_3 (not_3_out, replace);
  and and_1 (and_1_out, mem_en, decoder_1_out0);
  or or_1 (or_1_out, and_1_out, valid);
  not not_4 (not_4_out, replace);
  and and_2 (way0_en, not_3_out, or_1_out);
  and and_3 (way1_en, replace, or_1_out);
  and and_4 (block_wr_0, not_4_out, valid);
  and and_5 (block_wr_1, replace, valid);
  Comparator comparator_1 (.a(ram_2_data), .b({1'b1, tag}), .eq(comparator_1_eq));  // open: gt, lt
  or or_2 (hit, comparator_1_eq, way);
  Comparator comparator_2 (.a({1'b1, tag}), .b(ram_3_data), .eq(way));  // open: gt, lt
  Register #(.width(32)) Word_0 (.D(bus), .en(word0_en), .Q(Word_0_q), .clk(clk), .clr(reset));
  Register #(.width(32)) Word_1 (.D(bus), .en(word1_en), .Q(Word_1_q), .clk(clk), .clr(reset));
  Register #(.width(32)) Word_2 (.D(bus), .en(word2_en), .Q(Word_2_q), .clk(clk), .clr(reset));
  Register #(.width(32)) Word_3 (.D(bus), .en(word3_en), .Q(Word_3_q), .clk(clk), .clr(reset));
  RAM #(.addrWidth(5), .dataWidth(32), .bus("separate")) ram_4 (
    .addr(set), .din(Word_0_q), .data(ram_4_data), .str(block_wr_0), .clk(clk), .ld(hit), .clr(reset));  // open: sel
  RAM #(.addrWidth(5), .dataWidth(32), .bus("separate")) ram_5 (
    .addr(set), .din(Word_1_q), .data(ram_5_data), .str(block_wr_0), .clk(clk), .ld(hit), .clr(reset));  // open: sel
  RAM #(.addrWidth(5), .dataWidth(32), .bus("separate")) ram_6 (
    .addr(set), .din(Word_2_q), .data(ram_6_data), .str(block_wr_0), .clk(clk), .ld(hit), .clr(reset));  // open: sel
  RAM #(.addrWidth(5), .dataWidth(32), .bus("separate")) ram_7 (
    .addr(set), .din(Word_3_q), .data(ram_7_data), .str(block_wr_0), .clk(clk), .ld(hit), .clr(reset));  // open: sel
  RAM #(.addrWidth(5), .dataWidth(32), .bus("separate")) ram_8 (
    .addr(set), .din(Word_0_q), .data(ram_8_data), .str(block_wr_1), .clk(clk), .ld(hit), .clr(reset));  // open: sel
  RAM #(.addrWidth(5), .dataWidth(32), .bus("separate")) ram_9 (
    .addr(set), .din(Word_1_q), .data(ram_9_data), .str(block_wr_1), .clk(clk), .ld(hit), .clr(reset));  // open: sel
  RAM #(.addrWidth(5), .dataWidth(32), .bus("separate")) ram_10 (
    .addr(set), .din(Word_2_q), .data(ram_10_data), .str(block_wr_1), .clk(clk), .ld(hit), .clr(reset));  // open: sel
  RAM #(.addrWidth(5), .dataWidth(32), .bus("separate")) ram_11 (
    .addr(set), .din(Word_3_q), .data(ram_11_data), .str(block_wr_1), .clk(clk), .ld(hit), .clr(reset));  // open: sel
  Multiplexer #(.select(2), .width(32), .enable("false")) multiplexer_1 (
    .in0(ram_4_data), .in1(ram_5_data), .in2(ram_6_data), .in3(ram_7_data), .out(multiplexer_1_out),
    .sel(tunnel[3:2]));
  Multiplexer #(.select(2), .width(32), .enable("false")) multiplexer_2 (
    .in0(ram_8_data), .in1(ram_9_data), .in2(ram_10_data), .in3(ram_11_data), .out(multiplexer_2_out),
    .sel(tunnel[3:2]));
  Multiplexer #(.width(32), .enable("false")) multiplexer_3 (
    .in0(multiplexer_1_out), .in1(multiplexer_2_out), .out(Instr), .sel(way));

  // Other names for the same wires on the sheet: tunnel[15:4] = {tag, set}; word[3:0] = tunnel

  // Notes on the sheet:
  //   ROM Direcciones
  //   FIFO
  //   contents of rom_1 (hex, n*v repeats v):
  //   2000 1c04 8 c c144 4548 1f40 454c 5808 4a0c 6e00 4a00
  //   Tags/validez
  //   Via 0
  //   Via 1
  //   UC
  //   Almacenamiento
  //   Via 0
  //   Via 1
endmodule
