// Logisim project ejemplo uso tty.circ as structural Verilog: 1 circuit, main circuit main
module main (
  input  [6:0] in_1,
  input  in_2
);

  wire clk;

  Clock clock_1 (.out(clk));
  // tty_ctrl tty_ctrl_1: pin names not known
  // TTY tty_1: pin names not known; wires that end beside it: {16{1'b1}}, in_2, in_1, clk

  // Other names for the same wires on the sheet: D6_0[6:0] = in_1; en = in_2

  // Notes on the sheet:
  //   cte 0xffff
  //   permiso para imprimir en tty
  //   señal de reloj
  //   código ASCII 7 bits a imprimir en tty (0 borra pantalla)
endmodule
